// Logisim project hw5evolution.circ as structural Verilog: 13 circuits, main circuit MyXOR
module MyXOR (
);


  // Notes on the sheet:
  //   Here is a location to build an XOR circuit
  //   You can follow the tutorial (Help menu - "tutorial") or work on your own...
endmodule

module FullAdder (
  input  X,
  input  Y,
  input  CarryIn,
  output Sum,
  output CarryOut
);

  wire A1_out, A_out, B1_out, B_out, C1_out, C_out, D1_out, D_out, not_1_out, not_2_out, not_3_out;

  not not_1 (not_1_out, X);
  not not_2 (not_2_out, Y);
  not not_3 (not_3_out, CarryIn);
  and A (A_out, not_1_out, not_2_out, CarryIn);
  and B (B_out, not_1_out, Y, not_3_out);
  and C (C_out, X, not_2_out, not_3_out);
  and D (D_out, X, Y, CarryIn);
  and A1 (A1_out, not_1_out, Y, CarryIn);
  and B1 (B1_out, X, not_2_out, CarryIn);
  and C1 (C1_out, X, Y, not_3_out);
  and D1 (D1_out, X, Y, CarryIn);
  or or_1 (Sum, A_out, B_out, C_out, D_out);
  or or_2 (CarryOut, A1_out, B1_out, C1_out, D1_out);

  // Notes on the sheet:
  //   3 input bits:  X,  Y,  and CarryIn
  //   Here is a location to build an FULL ADDER circuit
  //   (1) draw the other four rails   (2) you'll need 8 AND gates    (3)  you'll need 2 OR gates
  //   two output bits:  Sum and CarryOut
endmodule

module A_4bit_Ripple_Carry_Adder (
  input  Y3,
  input  Y2,
  input  Y1,
  input  Y0,
  input  X3,
  input  X2,
  input  X1,
  input  X0,
  output Sum4,
  output Sum3,
  output Sum2,
  output Sum1,
  output Sum0
);

  wire fulladder_2_carryout, fulladder_3_carryout, fulladder_4_carryout;

  FullAdder fulladder_1 (.X(Y3), .Y(X3), .CarryIn(fulladder_2_carryout), .Sum(Sum3), .CarryOut(Sum4));
  FullAdder fulladder_2 (.X(Y2), .Y(X2), .CarryIn(fulladder_3_carryout), .Sum(Sum2), .CarryOut(fulladder_2_carryout));
  FullAdder fulladder_3 (.X(Y1), .Y(X1), .CarryIn(fulladder_4_carryout), .Sum(Sum1), .CarryOut(fulladder_3_carryout));
  FullAdder fulladder_4 (.X(Y0), .Y(X0), .CarryIn(1'b0), .Sum(Sum0), .CarryOut(fulladder_4_carryout));

  // Notes on the sheet:
  //   Here is a location to build an 4-bit RIPPLE-CARRY ADDER circuit
  //   8 input bits
  //   5 output bits
  //   Sad Ripple-Carry Adder
endmodule

module A_4bit_Multiplier (
  input  Y3,
  input  Y2,
  input  Y1,
  input  Y0,
  input  X3,
  input  X2,
  input  X1,
  input  X0,
  output Z7,
  output Z6,
  output Z5,
  output Z4,
  output Z3,
  output Z2,
  output Z1,
  output Z0
);

  wire a_4bit_ripple_carry_adder_1_sum1, a_4bit_ripple_carry_adder_1_sum2, a_4bit_ripple_carry_adder_1_sum3,
       a_4bit_ripple_carry_adder_1_sum4, a_4bit_ripple_carry_adder_2_sum1, a_4bit_ripple_carry_adder_2_sum2,
       a_4bit_ripple_carry_adder_2_sum3, a_4bit_ripple_carry_adder_2_sum4, a_4x1_multiplier_1_z0,
       a_4x1_multiplier_1_z1, a_4x1_multiplier_1_z2, a_4x1_multiplier_1_z3, a_4x1_multiplier_2_z0,
       a_4x1_multiplier_2_z1, a_4x1_multiplier_2_z2, a_4x1_multiplier_2_z3, a_4x1_multiplier_3_z0,
       a_4x1_multiplier_3_z1, a_4x1_multiplier_3_z2, a_4x1_multiplier_3_z3, a_4x1_multiplier_4_z0,
       a_4x1_multiplier_4_z1, a_4x1_multiplier_4_z2;

  A_4x1_multiplier a_4x1_multiplier_1 (
    .X3(Y3), .X2(Y2), .X1(Y1), .X0(Y0), .Y0(X0), .Z3(a_4x1_multiplier_1_z3), .Z2(a_4x1_multiplier_1_z2),
    .Z1(a_4x1_multiplier_1_z1), .Z0(a_4x1_multiplier_1_z0));
  A_4x1_multiplier a_4x1_multiplier_2 (
    .X3(Y3), .X2(Y2), .X1(Y1), .X0(Y0), .Y0(X1), .Z3(a_4x1_multiplier_2_z3), .Z2(a_4x1_multiplier_2_z2),
    .Z1(a_4x1_multiplier_2_z1), .Z0(a_4x1_multiplier_2_z0));
  A_4x1_multiplier a_4x1_multiplier_3 (
    .X3(Y3), .X2(Y2), .X1(Y1), .X0(Y0), .Y0(X2), .Z3(a_4x1_multiplier_3_z3), .Z2(a_4x1_multiplier_3_z2),
    .Z1(a_4x1_multiplier_3_z1), .Z0(a_4x1_multiplier_3_z0));
  A_4x1_multiplier a_4x1_multiplier_4 (
    .X3(Y3), .X2(Y2), .X1(Y1), .X0(Y0), .Y0(X3), .Z3(Z0), .Z2(a_4x1_multiplier_4_z2),
    .Z1(a_4x1_multiplier_4_z1), .Z0(a_4x1_multiplier_4_z0));
  A_4bit_Ripple_Carry_Adder a_4bit_ripple_carry_adder_1 (
    .X3(a_4x1_multiplier_3_z0), .Y2(a_4x1_multiplier_4_z0), .X2(a_4x1_multiplier_3_z1),
    .Y1(a_4x1_multiplier_4_z1), .X1(a_4x1_multiplier_3_z2), .Y0(a_4x1_multiplier_4_z2),
    .X0(a_4x1_multiplier_3_z3), .Sum4(a_4bit_ripple_carry_adder_1_sum4),
    .Sum3(a_4bit_ripple_carry_adder_1_sum3), .Sum2(a_4bit_ripple_carry_adder_1_sum2),
    .Sum1(a_4bit_ripple_carry_adder_1_sum1), .Sum0(Z1));  // open: Y3
  A_4bit_Ripple_Carry_Adder a_4bit_ripple_carry_adder_2 (
    .Y3(a_4bit_ripple_carry_adder_1_sum4), .X3(a_4x1_multiplier_2_z0), .Y2(a_4bit_ripple_carry_adder_1_sum3),
    .X2(a_4x1_multiplier_2_z1), .Y1(a_4bit_ripple_carry_adder_1_sum2), .X1(a_4x1_multiplier_2_z2),
    .Y0(a_4bit_ripple_carry_adder_1_sum1), .X0(a_4x1_multiplier_2_z3),
    .Sum4(a_4bit_ripple_carry_adder_2_sum4), .Sum3(a_4bit_ripple_carry_adder_2_sum3),
    .Sum2(a_4bit_ripple_carry_adder_2_sum2), .Sum1(a_4bit_ripple_carry_adder_2_sum1), .Sum0(Z2));
  A_4bit_Ripple_Carry_Adder a_4bit_ripple_carry_adder_3 (
    .Y3(a_4bit_ripple_carry_adder_2_sum4), .X3(a_4x1_multiplier_1_z0), .Y2(a_4bit_ripple_carry_adder_2_sum3),
    .X2(a_4x1_multiplier_1_z1), .Y1(a_4bit_ripple_carry_adder_2_sum2), .X1(a_4x1_multiplier_1_z2),
    .Y0(a_4bit_ripple_carry_adder_2_sum1), .X0(a_4x1_multiplier_1_z3), .Sum4(Z7), .Sum3(Z6), .Sum2(Z5),
    .Sum1(Z4), .Sum0(Z3));

  // Notes on the sheet:
  //   factor (4 bits)
  //   See the problem for details on this hint:   Build a 4x1-bit multiplier first!
  //   second factor (4 bits)
  //   product (8 bits)
  //   4-bit MULTIPLIER circuit
  //   most significant (highest) output bit
  //   least significant (lowest) output bit
endmodule

module A_3by2_divider (
  input  Y2,
  input  Y1,
  input  Y0,
  input  X1,
  input  X0,
  output Z2,
  output Z1,
  output Z0,
  output Error
);

  wire a_divisor_1_1_z0, a_divisor_1_1_z1, a_divisor_1_1_z2, a_divisor_2_1_z0, a_divisor_2_1_z1,
       a_divisor_2_1_z2, a_divisor_3_1_out_6, a_divisor_3_1_out_7, a_divisor_3_1_out_8, not_1_out, not_2_out;

  A_Divisor_1 a_divisor_1_1 (
    .Y2(Y2), .Y1(Y1), .Y0(Y0), .X1(X1), .X0(X0), .Z2(a_divisor_1_1_z2), .Z1(a_divisor_1_1_z1),
    .Z0(a_divisor_1_1_z0));  // open: Error
  A_Divisor_2 a_divisor_2_1 (
    .Y2(Y2), .Y1(Y1), .Y0(Y0), .X1(X1), .X0(X0), .Z2(a_divisor_2_1_z2), .Z1(a_divisor_2_1_z1),
    .Z0(a_divisor_2_1_z0));  // open: Error
  A_Divisor_3 a_divisor_3_1 (
    .in_1(Y2), .in_2(Y1), .in_3(Y0), .in_4(X1), .in_5(X0), .out_6(a_divisor_3_1_out_6),
    .out_7(a_divisor_3_1_out_7), .out_8(a_divisor_3_1_out_8));  // open: Error
  not not_1 (not_1_out, X1);
  not not_2 (not_2_out, X0);
  or or_1 (Z2, a_divisor_1_1_z2, a_divisor_2_1_z2, a_divisor_3_1_out_6);
  or or_2 (Z1, a_divisor_1_1_z1, a_divisor_2_1_z1, a_divisor_3_1_out_7);
  or or_3 (Z0, a_divisor_1_1_z0, a_divisor_2_1_z0, a_divisor_3_1_out_8);
  and and_1 (Error, not_1_out, not_2_out);

  // Notes on the sheet:
  //   Dividend (3 bits: Y2 Y1 Y0)
  //   Divisor (2 bits: X1 X0)
  //   Quotient (4 bits: Z2 Z1 Z0 and Error)
  //   3-by-2-bit DIVIDER circuit
endmodule

module A_2bit_decoder (
  input  in_1,
  input  in_2,
  output out_3,
  output out_4,
  output out_5,
  output out_6
);

  wire not_1_out, not_2_out;

  not not_1 (not_1_out, in_1);
  not not_2 (not_2_out, in_2);
  and and_1 (out_3, not_2_out, not_1_out);
  and and_2 (out_4, in_2, not_1_out);
  and and_3 (out_5, not_2_out, in_1);
  and and_4 (out_6, in_2, in_1);

  // Notes on the sheet:
  //   2-bit DECODER circuit (extra credit - see hw)
endmodule

module A_12nGb_memory (
);


  // Notes on the sheet:
  //   12 nanogigabit MEMORY circuit (extra credit - see hw)
endmodule

module A_4x1_multiplier (
  input  X3,
  input  X2,
  input  X1,
  input  X0,
  input  Y0,
  output Z3,
  output Z2,
  output Z1,
  output Z0
);

  and and_1 (Z3, X3, Y0);
  and and_2 (Z2, X2, Y0);
  and and_3 (Z1, X1, Y0);
  and and_4 (Z0, X0, Y0);
endmodule

module A_Divisor_1 (
  input  Y2,
  input  Y1,
  input  Y0,
  input  X1,
  input  X0,
  output Z2,
  output Z1,
  output Z0,
  output Error
);

  wire and_1_out, not_1_out;

  not not_1 (not_1_out, X1);
  and and_1 (and_1_out, not_1_out, X0);
  and and_2 (Z2, and_1_out, Y2);
  and and_3 (Z1, and_1_out, Y1);
  and and_4 (Z0, and_1_out, Y0);

  // Notes on the sheet:
  //   Dividend (3 bits: Y2 Y1 Y0)
  //   Divisor (2 bits: X1 X0)
  //   Quotient (4 bits: Z2 Z1 Z0 and Error)
  //   3-by-2-bit DIVIDER circuit
endmodule

module A_Divisor_2 (
  input  Y2,
  input  Y1,
  input  Y0,
  input  X1,
  input  X0,
  output Z2,
  output Z1,
  output Z0,
  output Error
);

  wire and_1_out, not_1_out;

  and and_1 (and_1_out, not_1_out, X1);
  not not_1 (not_1_out, X0);
  and and_2 (Z2, and_1_out, 1'b0, 1'b0);
  and and_3 (Z1, and_1_out, Y2);
  and and_4 (Z0, and_1_out, Y1);

  // Notes on the sheet:
  //   Dividend (3 bits: Y2 Y1 Y0)
  //   Divisor (2 bits: X1 X0)
  //   Quotient (4 bits: Z2 Z1 Z0 and Error)
  //   3-by-2-bit DIVIDER circuit
endmodule

module A_Divisor_3 (
  input  in_1,
  input  in_2,
  input  in_3,
  input  in_4,
  input  in_5,
  output out_6,
  output out_7,
  output out_8,
  output Error
);

  wire and_1_out, and_2_out, and_3_out, and_4_out, and_5_out, and_6_out, and_7_out, not_1_out, not_2_out,
       not_3_out, or_1_out, or_2_out;

  not not_1 (not_1_out, in_2);
  and and_1 (and_1_out, in_1, not_1_out);
  and and_2 (and_2_out, in_1, in_3);
  or or_1 (or_1_out, and_1_out, and_2_out, and_3_out);
  and and_3 (and_3_out, in_2, in_3);
  and and_4 (and_4_out, in_2, in_1);
  and and_5 (and_5_out, in_3, in_2, in_1);
  and and_6 (and_6_out, in_3, in_2, in_1);
  or or_2 (or_2_out, and_5_out, and_4_out);
  not not_2 (not_2_out, and_6_out);
  and and_7 (and_7_out, not_2_out, or_1_out);
  not not_3 (not_3_out, in_4);
  and and_8 (out_6, in_4, not_3_out);
  and and_9 (out_7, in_5, in_4, or_2_out);
  and and_10 (out_8, in_5, in_4, and_7_out);

  // Notes on the sheet:
  //   Dividend (3 bits: Y2 Y1 Y0)
  //   Divisor (2 bits: X1 X0)
  //   Quotient (4 bits: Z2 Z1 Z0 and Error)
endmodule

module SR_Latch (
  input  S,
  input  R,
  output out_3
);

  wire nor_1_out;

  nor nor_1 (nor_1_out, S, out_3);
  nor nor_2 (out_3, nor_1_out, R);
endmodule

module Flip_flop (
  input  in_1,
  input  in_2,
  output out_3
);

  wire and_1_out, and_2_out, not_1_out;

  not not_1 (not_1_out, in_1);
  and and_1 (and_1_out, in_1, in_2);
  and and_2 (and_2_out, not_1_out, in_2);
  SR_Latch sr_latch_1 (.S(and_1_out), .R(and_2_out), .out_3(out_3));

  // Notes on the sheet:
  //   Don't ask...
endmodule
